# Fritzing sketch Schematics (saved by Fritzing 0.9.3b)
breadboards: 1

parts:
  Componente1 = Arduino Leonardo (Rev3b)
  U1 = LM 358 Dual Op-Amp [part_number=MCP6022 package="SO 08 [SMD]"]
  R4 = Resistor [tolerance=±5% resistance=6k package=THT]
  Rs = Resistor [tolerance=±5% resistance=6.7k package=THT]
  LDR = Photocell (LDR) [package=THT]
  R1A/2 = Resistor [tolerance=±5% resistance=100k package="2512 [SMD]"]
  R1A/2_2 = Resistor [tolerance=±5% resistance=100k package="2512 [SMD]"]
  R1A/2_3 = Resistor [tolerance=±5% resistance=100k package="2512 [SMD]"]
  R1A/2_4 = Resistor [tolerance=±5% resistance=100k package="2512 [SMD]"]
  R2A = Resistor [tolerance=±5% resistance=1M package="2512 [SMD]"]
  R2A_2 = Resistor [tolerance=±5% resistance=1M package="2512 [SMD]"]
  SP1 = SPEAKER [package=pcb_mount_speaker]
  R1 = Resistor [tolerance=±5% resistance=10k package=THT]

nets (from the schematic view):
  N1: Componente1.D2/SDA, SP1.-
  N2: Componente1.5V, U1.connector3, Rs.Pin_0, R1.Pin_0
  N3: Componente1.GND, U1.connector7, R4.Pin_1, LDR.pin_1, R2A.Pin_0, SP1.+
  N4: Componente1.A0, U1.connector0, R2A_2.Pin_1
  N5: U1.connector1, R1A/2_2.Pin_0, R2A_2.Pin_0
  N6: U1.connector2, R1A/2_4.Pin_0, R2A.Pin_1
  N7: R4.Pin_0, R1A/2.Pin_0, R1.Pin_1
  N8: Rs.Pin_1, LDR.pin_0, R1A/2_3.Pin_0
  N9: R1A/2.Pin_1, R1A/2_2.Pin_1
  N10: R1A/2_3.Pin_1, R1A/2_4.Pin_1
